# Fritzing sketch Arduino_DIP_SW (saved by Fritzing 0.9.4)
breadboards: 2

parts:
  SW2 = DIP Switch 8 Position [package=dipswitch-08]
  パーツ1 = Arduino Pro Mini v13
  D1 = Rectifier Diode [part_number=1N4001 package="300 mil [THT]"]
  R2 = Resistor [tolerance=±5% resistance=330 package=THT]
  C1 = Electrolytic Capacitor [capacitance=1µF package="100 mil [THT, electrolytic]"]
  R3 = Resistor [tolerance=±5% resistance=220 package=THT]
  LED1 = LED - 5mm [color="Red (633nm)" package="5 mm [THT]"]
  R4 = Rotary Potentiometer (Small) [maximum_resistance=100kΩ package=THT]

nets:
  N1: SW2.1, パーツ1.D10_PWM/SS
  N2: SW2.2, パーツ1.D9_PWM
  N3: SW2.3, パーツ1.D8
  N4: SW2.4, パーツ1.D7
  N5: SW2.5, パーツ1.D6_PWM
  N6: SW2.6, パーツ1.D5_PWM
  N7: SW2.7, パーツ1.D4
  N8: SW2.8, パーツ1.D3_PWM
  N9: SW2.9, SW2.10, SW2.11, SW2.12, SW2.13, SW2.14, SW2.15, SW2.16, パーツ1.GND, D1.anode, C1.-, LED1.cathode, R4.leg1
  N10: パーツ1.VCC, C1.+, R4.leg2
  N11: パーツ1.A0, R4.wiper
  N12: パーツ1.D11_PWM/MOSI, R3.Pin_1
  N13: パーツ1.D2, D1.cathode, R2.Pin_0
  N14: R3.Pin_0, LED1.anode

notes:
  Sync In
  Gate Out
  ZENER
  5V
  GND
  +5V
  Duty
