# Fritzing sketch MCP23S17_DIP_SW (saved by Fritzing 0.9.4)
breadboards: 3

parts:
  IC1 = IC, DIP package, 28 pins [chip_label=MCP23S17]
  SW1 = DIP Switch 8 Position [package=dipswitch-08]
  SW2 = DIP Switch 8 Position [package=dipswitch-08]
  パーツ1 = Arduino Nano (Rev3.0)
  C1 = Ceramic Capacitor [capacitance=100nF package="100 mil [THT, multilayer]"]
  C2 = Electrolytic Capacitor [capacitance=1µF package="100 mil [THT, electrolytic]"]

nets:
  N1: IC1.pin1, SW2.16
  N2: IC1.pin2, SW2.15
  N3: IC1.pin3, SW2.14
  N4: IC1.pin4, SW2.13
  N5: IC1.pin5, SW2.12
  N6: IC1.pin6, SW2.11
  N7: IC1.pin7, SW2.10
  N8: IC1.pin8, SW2.9
  N9: IC1.pin9, パーツ1.5V, C1.0, C2.+
  N10: IC1.pin10, IC1.pin15, IC1.pin16, IC1.pin17, SW1.1, SW1.2, SW1.3, SW1.4, SW1.5, SW1.6, SW1.7, SW1.8, SW2.1, SW2.2, SW2.3, SW2.4, SW2.5, SW2.6, SW2.7, SW2.8, パーツ1.GND, C1.1, C2.-
  N11: IC1.pin11, パーツ1.D10
  N12: IC1.pin12, パーツ1.D13/SCK
  N13: IC1.pin13, パーツ1.D11/MOSI
  N14: IC1.pin14, パーツ1.D12/MISO
  N15: IC1.pin18, パーツ1.RESET
  N16: IC1.pin20, パーツ1.D2
  N17: IC1.pin21, SW1.16
  N18: IC1.pin22, SW1.15
  N19: IC1.pin23, SW1.14
  N20: IC1.pin24, SW1.13
  N21: IC1.pin25, SW1.12
  N22: IC1.pin26, SW1.11
  N23: IC1.pin27, SW1.10
  N24: IC1.pin28, SW1.9

notes:
  MCP23S17
  1 GPB0 28 GPA7
  2 GPB1 27 GPA6
  3 GPB2 26 GPA5
  4 GPB3 25 GPA4
  5 GPB4 24 GPA3
  6 GPB5 23 GPA2
  7 GPB6 22 GPA1
  8 GPB7 21 GPA0
  9 VDD 20 INTA
  10 VSS 19 INTB
  11 !CS 18 !RESET
  12 SCK 17 A2
  13 SI 16 A1
  14 SO 15 A0
